# Fritzing sketch nodeMCU-DS18B20 (saved by Fritzing 0.9.2b)
breadboards: 1

parts:
  U1 = NodeMCU V1.0
  VCC1 = 4 x AAA Battery Mount
  DD0503MA = mystery part, 3 pins [chip_label=3.7V]
  DS2 = DS18B20 1-Wire Temperature Sensor Probe Cable

nets:
  N1: U1.D0, U1.RST
  N2: U1.D4, DS2.DQ
  3V3: U1.3V3, DD0503MA.pin1, DS2.VDD
  GND: U1.GND, VCC1.-, DD0503MA.pin2, DS2.GND
  N3: VCC1.+, DD0503MA.pin3

notes:
  DD0503MA Ultra Small mini DC 3.7V 4.2V 4.5V 5V 6V to 3.3V Step Down Buck Regulator Module for 18650 ESP8266 breadboard

custom parts:
  NodeMCU V1.0: ESP9266 based NodeMCU
