# Fritzing sketch nodeMCU-teleinfo (saved by Fritzing 0.9.2b)
breadboards: 1

parts:
  U1 = NodeMCU V1.0
  VCC1 = 4 x AAA Battery Mount
  DD0503MA = mystery part, 3 pins [chip_label=3.7V]
  R1 = Resistor [tolerance=±5% resistance=103 package=THT]
  R2 = Resistor [tolerance=±5% resistance=103 package=THT]
  U2 = TLP621 [package=THT]

nets:
  N1: U1.D0, U1.RST
  N2: U1.3V3, DD0503MA.pin1, R1.Pin_1
  N3: U1.GND, VCC1.-, DD0503MA.pin2, U2.Pin_1
  N4: U1.D8, R1.Pin_0, U2.Pin_2
  N5: VCC1.+, DD0503MA.pin3
  N6: R2.Pin_0, U2.Pin_3

notes:
  i1
  i2

custom parts:
  NodeMCU V1.0: ESP9266 based NodeMCU
