# Fritzing sketch nodeMCU-GY-68 (saved by Fritzing 0.9.2b)
breadboards: 1

parts:
  U1 = NodeMCU V1.0
  VCC1 = 4 x AAA Battery Mount
  DD0503MA = mystery part, 3 pins [chip_label=3.7V]
  Composant1 = Barometric Pressure Sensor - BMP085 Breakout

nets:
  N1: U1.D0, U1.RST
  N2: U1.D1, Composant1.SCL
  N3: U1.D2, Composant1.SDA
  3V3: U1.3V3, DD0503MA.pin1, Composant1.VCC
  GND: U1.GND, VCC1.-, DD0503MA.pin2, Composant1.GND
  N4: VCC1.+, DD0503MA.pin3

custom parts:
  NodeMCU V1.0: ESP9266 based NodeMCU
