# Fritzing sketch nodeMCU-gps (saved by Fritzing 0.9.2b)
breadboards: 1

parts:
  VCC1 = 4 x AAA Battery Mount
  U1 = NEO 6M GPS
  U2 = NodeMCU V1.0

nets:
  GND: VCC1.-, U1.GND, U2.GND
  VCC: VCC1.+, U1.VCC, U2.3V3
  N1: U1.RXD, U2.D1
  N2: U1.TXD, U2.D2

custom parts:
  NEO 6M GPS: uSD module
  NodeMCU V1.0: ESP9266 based NodeMCU
