# Fritzing sketch nodeMCU-dht11 (saved by Fritzing 0.9.2b)
breadboards: 1

parts:
  DHT1 = DHT11 Humitidy and Temperature Sensor
  U1 = NodeMCU V1.0
  VCC1 = 4 x AAA Battery Mount
  DD0503MA = mystery part, 3 pins [chip_label=3.7V]

nets:
  VDD: DHT1.VDD, U1.3V3, DD0503MA.pin1
  N1: DHT1.DATA, U1.D1
  GND: DHT1.GND, U1.GND, VCC1.-, DD0503MA.pin2
  N2: U1.D0, U1.RST
  N3: VCC1.+, DD0503MA.pin3

notes:
  DD0503MA Ultra Small mini DC 3.7V 4.2V 4.5V 5V 6V to 3.3V Step Down Buck Regulator Module for 18650 ESP8266 breadboard

custom parts:
  DHT11 Humitidy and Temperature Sensor: DHT11 Humidity and Temperature Sensor
  NodeMCU V1.0: ESP9266 based NodeMCU
